# Fritzing sketch Sensor Module Schematic (saved by Fritzing 0.9.10b)

parts:
  LCD_Display_-_20x4 = LCD-16X2 [package=lcd-16x2_noholes]
  ESP32_Microcontroller = Heltec WiFi LoRa 32 V2 [part_number=HTIT-WB32LA]
  Buzzer = Passive Buzzer
  MG-811_Gas_Sensor = Header 5 [package=1x05-1mm]
  Mute_Switch = SWITCH_SPDT [package=kps-1290]
  Micro_SD_Card = microSD Socket [package=micro-sd-socket-pp]

nets:
  GND: LCD_Display_-_20x4.VSS, ESP32_Microcontroller.GND, Buzzer.-, MG-811_Gas_Sensor.5, Micro_SD_Card.GND
  VDD: LCD_Display_-_20x4.VDD, ESP32_Microcontroller.pin_20, MG-811_Gas_Sensor.4, Micro_SD_Card.VCC
  N1: LCD_Display_-_20x4.RS, ESP32_Microcontroller.pin_32
  N2: LCD_Display_-_20x4.R_W, ESP32_Microcontroller.pin_33
  N3: LCD_Display_-_20x4.DB0, LCD_Display_-_20x4.DB1, LCD_Display_-_20x4.DB2, LCD_Display_-_20x4.DB3, LCD_Display_-_20x4.DB4, LCD_Display_-_20x4.DB5, LCD_Display_-_20x4.DB6, LCD_Display_-_20x4.DB7, LCD_Display_-_20x4.A, LCD_Display_-_20x4.K
  N4: ESP32_Microcontroller.pin_5, Mute_Switch.P
  N5: ESP32_Microcontroller.pin_10, Micro_SD_Card.CS
  N6: ESP32_Microcontroller.pin_11, Micro_SD_Card.DO
  N7: ESP32_Microcontroller.pin_12, Micro_SD_Card.DI
  N8: ESP32_Microcontroller.pin_13, Micro_SD_Card.SCK
  N9: ESP32_Microcontroller.pin_14, MG-811_Gas_Sensor.2
  N10: Buzzer.S, Mute_Switch.S

notes:
  Key
  Red - VCC
  Black - GND
  Green/Yellow - SPI
  Blue - Digital Signal
